// Logisim project 21bit_ALU_2407112 (Correction).circ as structural Verilog: 10 circuits, main circuit main
module main (
  input  [1:0] Control,
  input  [20:0] in_2,
  input  [20:0] in_3,
  output [20:0] out_4,
  output Zero_Flag,
  output out_6,
  output Overflow_Flag,
  output Carry_Flag
);

  _21bit_ALU u_21bit_alu_1 (
    .in_3(in_2), .in_4(in_3), .out_5(out_4), .Zero_Flag(Zero_Flag), .out_7(out_6),
    .Overflow_Flag(Overflow_Flag), .Carry_Flag(Carry_Flag), .Control_1_Bit(Control[1]),
    .Control_0_Bit(Control[0]));

  // Notes on the sheet:
  //   A
  //   B
  //   Result
  //   Negative/ Sign Flag
endmodule

module Full_Adder (
  input  in_1,
  input  in_2,
  input  in_3,
  output out_4,
  output out_5
);

  wire and_1_out, and_2_out, xor_1_out;

  xor xor_1 (xor_1_out, in_2, in_3);
  and and_1 (and_1_out, in_2, in_3);
  and and_2 (and_2_out, in_1, xor_1_out);
  xor xor_2 (out_4, in_1, xor_1_out);
  or or_1 (out_5, and_2_out, and_1_out);
endmodule

// FA 21
module _21bit_full_adder (
  input  in_1,
  input  [20:0] in_2,
  input  [20:0] in_3,
  output [20:0] out_4,
  output out_5
);

  wire full_adder_1_out_5, full_adder_2_out_5, full_adder_3_out_5, full_adder_4_out_5, full_adder_5_out_5,
       full_adder_6_out_5, full_adder_7_out_5, full_adder_8_out_5, full_adder_9_out_5, full_adder_10_out_5,
       full_adder_11_out_5, full_adder_12_out_5, full_adder_13_out_5, full_adder_14_out_5,
       full_adder_15_out_5, full_adder_16_out_5, full_adder_17_out_5, full_adder_18_out_5,
       full_adder_19_out_5, full_adder_20_out_5;

  Full_Adder full_adder_1 (.in_1(in_1), .in_2(in_2[0]), .in_3(in_3[0]), .out_4(out_4[0]), .out_5(full_adder_1_out_5));
  Full_Adder full_adder_2 (
    .in_1(full_adder_1_out_5), .in_2(in_2[1]), .in_3(in_3[1]), .out_4(out_4[1]), .out_5(full_adder_2_out_5));
  Full_Adder full_adder_3 (
    .in_1(full_adder_2_out_5), .in_2(in_2[2]), .in_3(in_3[2]), .out_4(out_4[2]), .out_5(full_adder_3_out_5));
  Full_Adder full_adder_4 (
    .in_1(full_adder_3_out_5), .in_2(in_2[3]), .in_3(in_3[3]), .out_4(out_4[3]), .out_5(full_adder_4_out_5));
  Full_Adder full_adder_5 (
    .in_1(full_adder_4_out_5), .in_2(in_2[4]), .in_3(in_3[4]), .out_4(out_4[4]), .out_5(full_adder_5_out_5));
  Full_Adder full_adder_6 (
    .in_1(full_adder_5_out_5), .in_2(in_2[5]), .in_3(in_3[5]), .out_4(out_4[5]), .out_5(full_adder_6_out_5));
  Full_Adder full_adder_7 (
    .in_1(full_adder_6_out_5), .in_2(in_2[6]), .in_3(in_3[6]), .out_4(out_4[6]), .out_5(full_adder_7_out_5));
  Full_Adder full_adder_8 (
    .in_1(full_adder_7_out_5), .in_2(in_2[7]), .in_3(in_3[7]), .out_4(out_4[7]), .out_5(full_adder_8_out_5));
  Full_Adder full_adder_9 (
    .in_1(full_adder_8_out_5), .in_2(in_2[8]), .in_3(in_3[8]), .out_4(out_4[8]), .out_5(full_adder_9_out_5));
  Full_Adder full_adder_10 (
    .in_1(full_adder_9_out_5), .in_2(in_2[9]), .in_3(in_3[9]), .out_4(out_4[9]), .out_5(full_adder_10_out_5));
  Full_Adder full_adder_11 (
    .in_1(full_adder_10_out_5), .in_2(in_2[10]), .in_3(in_3[10]), .out_4(out_4[10]),
    .out_5(full_adder_11_out_5));
  Full_Adder full_adder_12 (
    .in_1(full_adder_11_out_5), .in_2(in_2[11]), .in_3(in_3[11]), .out_4(out_4[11]),
    .out_5(full_adder_12_out_5));
  Full_Adder full_adder_13 (
    .in_1(full_adder_12_out_5), .in_2(in_2[12]), .in_3(in_3[12]), .out_4(out_4[12]),
    .out_5(full_adder_13_out_5));
  Full_Adder full_adder_14 (
    .in_1(full_adder_13_out_5), .in_2(in_2[13]), .in_3(in_3[13]), .out_4(out_4[13]),
    .out_5(full_adder_14_out_5));
  Full_Adder full_adder_15 (
    .in_1(full_adder_14_out_5), .in_2(in_2[14]), .in_3(in_3[14]), .out_4(out_4[14]),
    .out_5(full_adder_15_out_5));
  Full_Adder full_adder_16 (
    .in_1(full_adder_15_out_5), .in_2(in_2[15]), .in_3(in_3[15]), .out_4(out_4[15]),
    .out_5(full_adder_16_out_5));
  Full_Adder full_adder_17 (
    .in_1(full_adder_16_out_5), .in_2(in_2[16]), .in_3(in_3[16]), .out_4(out_4[16]),
    .out_5(full_adder_17_out_5));
  Full_Adder full_adder_18 (
    .in_1(full_adder_17_out_5), .in_2(in_2[17]), .in_3(in_3[17]), .out_4(out_4[17]),
    .out_5(full_adder_18_out_5));
  Full_Adder full_adder_19 (
    .in_1(full_adder_18_out_5), .in_2(in_2[18]), .in_3(in_3[18]), .out_4(out_4[18]),
    .out_5(full_adder_19_out_5));
  Full_Adder full_adder_20 (
    .in_1(full_adder_19_out_5), .in_2(in_2[19]), .in_3(in_3[19]), .out_4(out_4[19]),
    .out_5(full_adder_20_out_5));
  Full_Adder full_adder_21 (
    .in_1(full_adder_20_out_5), .in_2(in_2[20]), .in_3(in_3[20]), .out_4(out_4[20]), .out_5(out_5));
endmodule

// XOR
module _21bit_XOR (
  input  [20:0] in_1,
  input  [20:0] in_2,
  output [20:0] out_3
);

  xor xor_1 (out_3[0], in_1[0], in_2[0]);
  xor xor_2 (out_3[1], in_1[1], in_2[1]);
  xor xor_3 (out_3[2], in_1[2], in_2[2]);
  xor xor_4 (out_3[3], in_1[3], in_2[3]);
  xor xor_5 (out_3[4], in_1[4], in_2[4]);
  xor xor_6 (out_3[5], in_1[5], in_2[5]);
  xor xor_7 (out_3[6], in_1[6], in_2[6]);
  xor xor_8 (out_3[7], in_1[7], in_2[7]);
  xor xor_9 (out_3[8], in_1[8], in_2[8]);
  xor xor_10 (out_3[9], in_1[9], in_2[9]);
  xor xor_11 (out_3[10], in_1[10], in_2[10]);
  xor xor_12 (out_3[11], in_1[11], in_2[11]);
  xor xor_13 (out_3[12], in_1[12], in_2[12]);
  xor xor_14 (out_3[13], in_1[13], in_2[13]);
  xor xor_15 (out_3[14], in_1[14], in_2[14]);
  xor xor_16 (out_3[15], in_1[15], in_2[15]);
  xor xor_17 (out_3[16], in_1[16], in_2[16]);
  xor xor_18 (out_3[17], in_1[17], in_2[17]);
  xor xor_19 (out_3[18], in_1[18], in_2[18]);
  xor xor_20 (out_3[19], in_1[19], in_2[19]);
  xor xor_21 (out_3[20], in_1[20], in_2[20]);
endmodule

// ADD/SUB
module Add_or_Sub (
  input  Sub,
  input  [20:0] in_2,
  input  [20:0] in_3,
  output [20:0] out_4,
  output Carry,
  output overflow
);

  wire and_1_out, and_2_out, msb_bit_out_1_msb___sign_bit, msb_bit_out_2_msb___sign_bit,
       msb_bit_out_3_msb___sign_bit, not_1_out, not_2_out, not_3_out;
  wire [20:0] bit_extender_1_out, n21bit_xor_1_out_3;

  MSB_bit_Out msb_bit_out_1 (.in_1(in_2), .MSB___Sign_bit(msb_bit_out_1_msb___sign_bit));
  MSB_bit_Out msb_bit_out_2 (.in_1(n21bit_xor_1_out_3), .MSB___Sign_bit(msb_bit_out_2_msb___sign_bit));
  not not_1 (not_1_out, msb_bit_out_1_msb___sign_bit);
  not not_2 (not_2_out, msb_bit_out_2_msb___sign_bit);
  assign bit_extender_1_out = {{20{Sub}}, Sub};  // Bit_Extender bit_extender_1
  _21bit_XOR u_21bit_xor_1 (.in_1(bit_extender_1_out), .in_2(in_3), .out_3(n21bit_xor_1_out_3));
  _21bit_full_adder u_21bit_full_adder_1 (
    .in_1(Sub), .in_2(in_2), .in_3(n21bit_xor_1_out_3), .out_4(out_4), .out_5(Carry));
  MSB_bit_Out msb_bit_out_3 (.in_1(out_4), .MSB___Sign_bit(msb_bit_out_3_msb___sign_bit));
  not not_3 (not_3_out, msb_bit_out_3_msb___sign_bit);
  and and_1 (and_1_out, msb_bit_out_1_msb___sign_bit, msb_bit_out_2_msb___sign_bit, not_3_out);
  and and_2 (and_2_out, not_1_out, not_2_out, msb_bit_out_3_msb___sign_bit);
  or or_1 (overflow, and_1_out, and_2_out);
endmodule

// MSB
module MSB_bit_Out (
  input  [20:0] in_1,
  output MSB___Sign_bit
);


  assign MSB___Sign_bit = in_1[20];
endmodule

// 21 Bit AND
module _21bit_AND (
  input  [20:0] in_1,
  input  [20:0] in_2,
  output [20:0] out_3
);

  and and_1 (out_3[0], in_1[0], in_2[0]);
  and and_2 (out_3[1], in_1[1], in_2[1]);
  and and_3 (out_3[2], in_1[2], in_2[2]);
  and and_4 (out_3[3], in_1[3], in_2[3]);
  and and_5 (out_3[4], in_1[4], in_2[4]);
  and and_6 (out_3[5], in_1[5], in_2[5]);
  and and_7 (out_3[6], in_1[6], in_2[6]);
  and and_8 (out_3[7], in_1[7], in_2[7]);
  and and_9 (out_3[8], in_1[8], in_2[8]);
  and and_10 (out_3[9], in_1[9], in_2[9]);
  and and_11 (out_3[10], in_1[10], in_2[10]);
  and and_12 (out_3[11], in_1[11], in_2[11]);
  and and_13 (out_3[12], in_1[12], in_2[12]);
  and and_14 (out_3[13], in_1[13], in_2[13]);
  and and_15 (out_3[14], in_1[14], in_2[14]);
  and and_16 (out_3[15], in_1[15], in_2[15]);
  and and_17 (out_3[16], in_1[16], in_2[16]);
  and and_18 (out_3[17], in_1[17], in_2[17]);
  and and_19 (out_3[18], in_1[18], in_2[18]);
  and and_20 (out_3[19], in_1[19], in_2[19]);
  and and_21 (out_3[20], in_1[20], in_2[20]);
endmodule

// 21 Bit OR
module _21bit_OR (
  input  [20:0] in_1,
  input  [20:0] in_2,
  output [20:0] out_3
);

  or or_1 (out_3[0], in_1[0], in_2[0]);
  or or_2 (out_3[1], in_1[1], in_2[1]);
  or or_3 (out_3[2], in_1[2], in_2[2]);
  or or_4 (out_3[3], in_1[3], in_2[3]);
  or or_5 (out_3[4], in_1[4], in_2[4]);
  or or_6 (out_3[5], in_1[5], in_2[5]);
  or or_7 (out_3[6], in_1[6], in_2[6]);
  or or_8 (out_3[7], in_1[7], in_2[7]);
  or or_9 (out_3[8], in_1[8], in_2[8]);
  or or_10 (out_3[9], in_1[9], in_2[9]);
  or or_11 (out_3[10], in_1[10], in_2[10]);
  or or_12 (out_3[11], in_1[11], in_2[11]);
  or or_13 (out_3[12], in_1[12], in_2[12]);
  or or_14 (out_3[13], in_1[13], in_2[13]);
  or or_15 (out_3[14], in_1[14], in_2[14]);
  or or_16 (out_3[15], in_1[15], in_2[15]);
  or or_17 (out_3[16], in_1[16], in_2[16]);
  or or_18 (out_3[17], in_1[17], in_2[17]);
  or or_19 (out_3[18], in_1[18], in_2[18]);
  or or_20 (out_3[19], in_1[19], in_2[19]);
  or or_21 (out_3[20], in_1[20], in_2[20]);
endmodule

// ZF
module Zero_checker (
  input  [20:0] in_1,
  output Zero_Flag
);

  wire or_1_out, or_2_out, or_3_out, or_4_out, or_5_out, or_6_out, or_7_out, or_8_out, or_9_out, or_10_out,
       or_11_out, or_12_out, or_13_out, or_14_out, or_15_out, or_16_out, or_17_out, or_18_out, or_19_out,
       or_20_out;

  or or_1 (or_1_out, in_1[0], in_1[1]);
  or or_2 (or_2_out, or_1_out, in_1[2]);
  or or_3 (or_3_out, in_1[6], in_1[7]);
  or or_4 (or_4_out, or_3_out, in_1[8]);
  or or_5 (or_5_out, in_1[11], in_1[12]);
  or or_6 (or_6_out, in_1[16], in_1[17]);
  or or_7 (or_7_out, or_2_out, in_1[3]);
  or or_8 (or_8_out, or_4_out, in_1[9]);
  or or_9 (or_9_out, or_5_out, in_1[13]);
  or or_10 (or_10_out, or_9_out, in_1[14]);
  or or_11 (or_11_out, or_6_out, in_1[18]);
  or or_12 (or_12_out, or_11_out, in_1[19]);
  or or_13 (or_13_out, or_7_out, in_1[4]);
  or or_14 (or_14_out, or_13_out, in_1[5]);
  or or_15 (or_15_out, or_8_out, in_1[10]);
  or or_16 (or_16_out, or_10_out, in_1[15]);
  or or_17 (or_17_out, or_12_out, in_1[20]);
  or or_18 (or_18_out, or_14_out, or_15_out);
  or or_19 (or_19_out, or_16_out, or_17_out);
  or or_20 (or_20_out, or_18_out, or_19_out);
  not not_1 (Zero_Flag, or_20_out);
endmodule

// 21 Bit ALU
module _21bit_ALU (
  input  Control_1_Bit,
  input  Control_0_Bit,
  input  [20:0] in_3,
  input  [20:0] in_4,
  output [20:0] out_5,
  output Zero_Flag,
  output out_7,
  output Overflow_Flag,
  output Carry_Flag
);

  wire add_or_sub_1_carry;
  wire [20:0] add_or_sub_1_out_4, multiplexer_1_out, n21bit_and_1_out_3, n21bit_or_1_out_3;

  _21bit_AND u_21bit_and_1 (.in_1(in_3), .in_2(in_4), .out_3(n21bit_and_1_out_3));
  _21bit_OR u_21bit_or_1 (.in_1(in_3), .in_2(in_4), .out_3(n21bit_or_1_out_3));
  Add_or_Sub add_or_sub_1 (
    .Sub(Control_0_Bit), .in_2(in_3), .in_3(in_4), .out_4(add_or_sub_1_out_4), .Carry(add_or_sub_1_carry),
    .overflow(Overflow_Flag));
  Multiplexer #(.width(21), .enable("false")) multiplexer_1 (
    .in0(n21bit_and_1_out_3), .in1(n21bit_or_1_out_3), .out(multiplexer_1_out), .sel(Control_0_Bit));
  and and_1 (Carry_Flag, Control_1_Bit, add_or_sub_1_carry);
  Multiplexer #(.width(21), .enable("false")) multiplexer_2 (
    .in0(multiplexer_1_out), .in1(add_or_sub_1_out_4), .out(out_5), .sel(Control_1_Bit));
  Zero_checker zero_checker_1 (.in_1(out_5), .Zero_Flag(Zero_Flag));
  MSB_bit_Out msb_bit_out_1 (.in_1(out_5), .MSB___Sign_bit(out_7));

  // Notes on the sheet:
  //   A
  //   B
  //   Control0 MUX
  //   Control1 MUX
  //   Result
  //   Negative/ Sign Flag
endmodule
