// Logisim project 21 bit register-to-register data transfer.circ as structural Verilog: 1 circuit, main circuit main
module main (
  input  [20:0] Input,
  input  Clear
);

  wire Clock_out;
  wire [1:0] counter_1_q;
  wire [6:0] rom_1_data;
  wire [20:0] A_q, B_q, C_q, D_q, multiplexer_1_out;

  Clock Clock (.out(Clock_out));
  Counter #(.width(2), .max('h3)) counter_1 (
    .Q(counter_1_q), .clk(Clock_out), .clr(Clear));  // open: load, D, count, carry
  ROM #(.addrWidth(2), .dataWidth(7)) rom_1 (.addr(counter_1_q), .data(rom_1_data), .sel(1'b1));
  Multiplexer #(.select(3), .width(21), .enable("false")) multiplexer_1 (
    .in0(Input), .in1(A_q), .in2(B_q), .in3(C_q), .in4(D_q), .out(multiplexer_1_out), .sel(rom_1_data[6:4]));  // open: in5, in6, in7
  Register #(.width(21)) A (.D(multiplexer_1_out), .en(rom_1_data[3]), .Q(A_q), .clk(Clock_out), .clr(Clear));
  Register #(.width(21)) B (.D(multiplexer_1_out), .en(rom_1_data[2]), .Q(B_q), .clk(Clock_out), .clr(Clear));
  Register #(.width(21)) C (.D(multiplexer_1_out), .en(rom_1_data[1]), .Q(C_q), .clk(Clock_out), .clr(Clear));
  Register #(.width(21)) D (.D(multiplexer_1_out), .en(rom_1_data[0]), .Q(D_q), .clk(Clock_out), .clr(Clear));

  // Notes on the sheet:
  //   contents of rom_1 (hex, n*v repeats v):
  //   8 14 21 42
endmodule
